# Fritzing sketch CouvertureChauffanteSchema (saved by Fritzing 0.8.7b)
circuit board: 15cm x 5.64cm
breadboards: 2

parts:
  Composant1 = Arduino Uno (Rev3)
  LCD1 = LCD screen
  S1 = Pushbutton [package="[THT]"]
  S2 = Pushbutton [package="[THT]"]
  S3 = Pushbutton [package="[THT]"]
  S4 = Pushbutton [package="[THT]"]
  R1 = Resistor [tolerance=±5% resistance=220 package=THT]
  R2 = Resistor [tolerance=±5% resistance=10k package=THT]
  R3 = Resistor [tolerance=±5% resistance=10k package=THT]
  R4 = Resistor [tolerance=±5% resistance=10k package=THT]
  IC1 = 24LC128 [package=THT]
  R5 = Resistor [tolerance=±5% resistance=10k package=THT]
  R6 = Resistor [tolerance=±5% resistance=10k package=THT]
  Q1 = NPN-Transistor [part_number=ZTX688B package="TO92 [THT]"]
  Q2 = NPN-Transistor [part_number=ZTX688B package="TO92 [THT]"]
  Q3 = NPN-Transistor [part_number=ZTX688B package="TO92 [THT]"]
  Q4 = NPN-Transistor [part_number=ZTX688B package="TO92 [THT]"]
  R7 = Temperature Sensor (Thermistor) [thermistor_type=NTC package=THT]
  R8 = Temperature Sensor (Thermistor) [thermistor_type=NTC package=THT]
  R9 = Temperature Sensor (Thermistor) [thermistor_type=NTC package=THT]
  R10 = Temperature Sensor (Thermistor) [thermistor_type=NTC package=THT]
  R11 = Resistor [tolerance=±5% resistance=10k package=THT]
  R12 = Resistor [tolerance=±5% resistance=10k package=THT]
  R13 = Resistor [tolerance=±5% resistance=10k package=THT]
  R14 = Resistor [tolerance=±5% resistance=10k package=THT]
  R15 = Resistor [tolerance=±5% resistance=1k package=THT]
  R16 = Resistor [tolerance=±5% resistance=1k package=THT]
  R17 = Resistor [tolerance=±5% resistance=1k package=THT]
  R18 = Resistor [tolerance=±5% resistance=1k package=THT]
  Composant2 = Arduino Nano (Rev3.0)  # not connected

nets:
  N1: Composant1.A0, S2.Pin_3, S2.Pin_4, R2.Pin_1
  N2: Composant1.A1, R10.pin_1, R14.Pin_0
  N3: Composant1.A2, R9.pin_1, R13.Pin_0
  N4: Composant1.A3, R8.pin_1, R12.Pin_0
  N5: Composant1.A4/SDA, IC1.SDA_-_I2C_Data, R6.Pin_1
  N6: Composant1.A5/SCL, IC1.SCL_-_I2C_Clock, R5.Pin_1
  N7: Composant1.D8, R16.Pin_1
  N8: Composant1.D9_PWM, R17.Pin_1
  N9: Composant1.D10_PWM/SS, R18.Pin_1
  N10: Composant1.D11_PWM/MOSI, LCD1.E
  N11: Composant1.D12/MISO, LCD1.RS
  GND: Composant1.GND, LCD1.VSS, LCD1.R/W, LCD1.LED-, S1.Pin_1, S1.Pin_2, S2.Pin_1, S2.Pin_2, S3.Pin_1, S3.Pin_2, S4.Pin_1, S4.Pin_2, IC1.0V, IC1.WP_-_Write_Protect, Q1.C, Q2.C, Q3.C, Q4.C, R11.Pin_1, R12.Pin_1, R13.Pin_1, R14.Pin_1
  N12: Composant1.D2, LCD1.DB7
  N13: Composant1.D3_PWM, LCD1.DB6
  N14: Composant1.D4, LCD1.DB5
  N15: Composant1.D5_PWM, LCD1.DB4
  N16: Composant1.D6_PWM, LCD1.V0
  N17: Composant1.D7, R15.Pin_1
  5V: Composant1.5V, LCD1.VDD, R1.Pin_1, IC1.+V, R5.Pin_0, R6.Pin_0, R7.pin_0, R9.pin_0, R10.pin_0
  N18: LCD1.LED+, R1.Pin_0
  N19: S1.Pin_3, S1.Pin_4, R2.Pin_0, R4.Pin_1
  N20: S3.Pin_3, S3.Pin_4, R3.Pin_1, R4.Pin_0
  N21: S4.Pin_3, S4.Pin_4, R3.Pin_0
  N22: Q1.E, Q2.E, Q3.E, Q4.E
  N23: Q1.B, R15.Pin_0
  N24: Q2.B, R16.Pin_0
  N25: Q3.B, R17.Pin_0
  N26: Q4.B, R18.Pin_0
  N27: R7.pin_1, R11.Pin_0
