# Fritzing sketch CouvertureChauffanteSchema_NewGen (saved by Fritzing 0.9.4)
circuit board: 13.3497cm x 4.74365cm
circuit board: 2.63854cm x 2.9499cm
breadboards: 2

parts:
  LCD_16x4 = LCD screen
  R1 = Resistor [tolerance=±5% resistance=220 package=THT]
  EEPROM = 24LC128 [package=THT]
  R5 = Resistor [tolerance=±5% resistance=10k package=THT]
  R6 = Resistor [tolerance=±5% resistance=10k package=THT]
  R11 = Resistor [tolerance=±5% resistance=10k package=THT]
  R12 = Resistor [tolerance=±5% resistance=10k package=THT]
  R13 = Resistor [tolerance=±5% resistance=10k package=THT]
  R14 = Resistor [tolerance=±5% resistance=10k package=THT]
  trFL = NPN-Transistor [package="TO92 [THT]"]
  trFR = NPN-Transistor [package="TO92 [THT]"]
  trRR = NPN-Transistor [package="TO92 [THT]"]
  trRL = NPN-Transistor [package="TO92 [THT]"]
  R15 = Resistor [tolerance=±5% resistance=1k package=THT]
  R16 = Resistor [tolerance=±5% resistance=1k package=THT]
  R17 = Resistor [tolerance=±5% resistance=1k package=THT]
  R18 = Resistor [tolerance=±5% resistance=1k package=THT]
  Arduino_Nano = Arduino Nano (Rev3.0)
  RPshBck = Resistor [tolerance=±5% resistance=10k package=THT]
  Dwn = Pushbutton [package="[THT]"]
  Up = Pushbutton [package="[THT]"]
  Val = Pushbutton [package="[THT]"]
  Bck = Pushbutton [package="[THT]"]
  RVal = Resistor [tolerance=±5% resistance=1k package=THT]
  RPshUp = Resistor [tolerance=±5% resistance=1k package=THT]
  RPshDwn = Resistor [tolerance=±5% resistance=1k package=THT]
  tRL+ = female pin header, 1 pin [form="♀ (female)"]
  pRL+ = female pin header, 1 pin [form="♀ (female)"]
  pRR+ = female pin header, 1 pin [form="♀ (female)"]
  tRR+ = female pin header, 1 pin [form="♀ (female)"]
  pRR- = female pin header, 1 pin [form="♀ (female)"]
  tRRs = female pin header, 1 pin [form="♀ (female)"]
  tRLs = female pin header, 1 pin [form="♀ (female)"]
  pRL- = female pin header, 1 pin [form="♀ (female)"]
  pFL- = female pin header, 1 pin [form="♀ (female)"]
  tFL+ = female pin header, 1 pin [form="♀ (female)"]
  tFLs = female pin header, 1 pin [form="♀ (female)"]
  pFL+ = female pin header, 1 pin [form="♀ (female)"]
  pFR+ = female pin header, 1 pin [form="♀ (female)"]
  tFRs = female pin header, 1 pin [form="♀ (female)"]
  pFR- = female pin header, 1 pin [form="♀ (female)"]
  tFR+ = female pin header, 1 pin [form="♀ (female)"]
  12v = Screw terminal - 2 pins [package=THT]
  J1 = female pin header, 2 pins [form="♀ (female)"]
  - = female pin header, 2 pins [form="♀ (female)"]
  J3 = Power Jack [package=power_jack_pth]  # not connected

nets:
  VSS: LCD_16x4.VSS, LCD_16x4.R/W, LCD_16x4.LED-, EEPROM.0V, EEPROM.WP_-_Write_Protect, R11.Pin_1, R12.Pin_1, R13.Pin_1, R14.Pin_1, trFL.E, trFR.E, trRR.E, trRL.E, Arduino_Nano.GND, Dwn.Pin_1, Dwn.Pin_2, Up.Pin_1, Up.Pin_2, Val.Pin_1, Val.Pin_2, Bck.Pin_1, Bck.Pin_2, 12v.pin1, -.pin2
  VDD: LCD_16x4.VDD, R1.Pin_1, EEPROM.+V, R5.Pin_0, R6.Pin_0, Arduino_Nano.5V, RPshBck.Pin_0, tRL+.pin1, tRR+.pin1, tFL+.pin1, tFR+.pin1
  N1: LCD_16x4.V0, Arduino_Nano.D6
  N2: LCD_16x4.RS, Arduino_Nano.D12/MISO
  N3: LCD_16x4.E, Arduino_Nano.D11/MOSI
  N4: LCD_16x4.DB4, Arduino_Nano.D5
  N5: LCD_16x4.DB5, Arduino_Nano.D4
  N6: LCD_16x4.DB6, Arduino_Nano.D3
  N7: LCD_16x4.DB7, Arduino_Nano.D2
  N8: LCD_16x4.LED+, R1.Pin_0
  N9: EEPROM.SDA_-_I2C_Data, R6.Pin_1, Arduino_Nano.A4
  N10: EEPROM.SCL_-_I2C_Clock, R5.Pin_1, Arduino_Nano.A5
  N11: R11.Pin_0, Arduino_Nano.A1, tFLs.pin1
  N12: R12.Pin_0, Arduino_Nano.A0, tFRs.pin1
  N13: R13.Pin_0, Arduino_Nano.A3, tRLs.pin1
  N14: R14.Pin_0, Arduino_Nano.A2, tRRs.pin1
  N15: trFL.B, R15.Pin_0
  N16: trFL.C, pFL-.pin1
  N17: trFR.B, R16.Pin_0
  N18: trFR.C, pFR-.pin1
  N19: trRR.B, R18.Pin_0
  N20: trRR.C, pRR-.pin1
  N21: trRL.B, R17.Pin_0
  N22: trRL.C, pRL-.pin1
  N23: R15.Pin_1, Arduino_Nano.D9
  N24: R16.Pin_1, Arduino_Nano.D10
  N25: R17.Pin_1, Arduino_Nano.D7
  N26: R18.Pin_1, Arduino_Nano.D8
  N27: Arduino_Nano.VIN, J1.pin1
  N28: Arduino_Nano.A6, RPshBck.Pin_1, Bck.Pin_3, Bck.Pin_4, RVal.Pin_0, -.pin1
  N29: Dwn.Pin_3, Dwn.Pin_4, RPshDwn.Pin_1
  N30: Up.Pin_3, Up.Pin_4, RPshUp.Pin_1, RPshDwn.Pin_0
  N31: Val.Pin_3, Val.Pin_4, RVal.Pin_1, RPshUp.Pin_0
  N32: pRL+.pin1, pRR+.pin1, pFL+.pin1, pFR+.pin1, 12v.pin2, J1.pin2

notes:
  +
  -
  -+
  UP
  Vin
  D13
  -unused-
